# Fritzing sketch AnalogRGB (saved by Fritzing 0.9.2b)
breadboards: 1

parts:
  Part1 = Arduino Uno (Rev3)
  R1 = Rotary Potentiometer (Small) [maximum_resistance=100kΩ package=THT]
  S1 = Pushbutton [package="[THT]"]
  S2 = Pushbutton [package="[THT]"]
  S3 = Pushbutton [package="[THT]"]
  R2 = Resistor [tolerance=±5% resistance=220 package=THT]
  R3 = Resistor [tolerance=±5% resistance=220 package=THT]
  R4 = Resistor [tolerance=±5% resistance=220 package=THT]
  LED1 = RGB LED (com. cathode, rgb) [package="5 mm [THT]"]
  R5 = Resistor [tolerance=±5% resistance=220 package=THT]
  R6 = Resistor [tolerance=±5% resistance=220 package=THT]
  R7 = Resistor [tolerance=±5% resistance=220 package=THT]

nets:
  N1: Part1.A0, R1.wiper
  N2: Part1.D9_PWM, R6.Pin_1
  N3: Part1.D10_PWM/SS, R5.Pin_1
  N4: Part1.D11_PWM/MOSI, R7.Pin_1
  N5: Part1.D5_PWM, S1.Pin_1, S1.Pin_2, R2.Pin_0
  N6: Part1.D6_PWM, S2.Pin_1, S2.Pin_2, R3.Pin_0
  N7: Part1.D7, S3.Pin_1, S3.Pin_2, R4.Pin_0
  N8: Part1.5V, R1.leg2, S1.Pin_3, S1.Pin_4, S2.Pin_3, S2.Pin_4, S3.Pin_3, S3.Pin_4, LED1.common_cathode
  N9: Part1.GND, R1.leg1, R2.Pin_1, R3.Pin_1, R4.Pin_1
  N10: LED1.red_anode, R6.Pin_0
  N11: LED1.green_anode, R5.Pin_0
  N12: LED1.blue_anode, R7.Pin_0
