# Fritzing sketch RGB (saved by Fritzing 0.9.2b)
breadboards: 1

parts:
  Part1 = Arduino Uno (Rev3)
  LED1 = RGB LED (com. cathode, rgb) [package="5 mm [THT]"]
  R1 = Resistor [tolerance=±5% resistance=220 package=THT]
  R2 = Resistor [tolerance=±5% resistance=220 package=THT]
  R3 = Resistor [tolerance=±5% resistance=220 package=THT]
  S1 = Pushbutton [package="[THT]"]
  S2 = Pushbutton [package="[THT]"]
  S3 = Pushbutton [package="[THT]"]
  R4 = Resistor [tolerance=±5% resistance=220 package=THT]
  R5 = Resistor [tolerance=±5% resistance=220 package=THT]
  R6 = Resistor [tolerance=±5% resistance=220 package=THT]

nets:
  N1: Part1.D8, S1.Pin_3, S1.Pin_4, R4.Pin_0
  N2: Part1.D9_PWM, S2.Pin_3, S2.Pin_4, R5.Pin_0
  N3: Part1.D10_PWM/SS, S3.Pin_3, S3.Pin_4, R6.Pin_0
  N4: Part1.D2, R1.Pin_1
  N5: Part1.D3_PWM, R2.Pin_1
  N6: Part1.D4, R3.Pin_1
  N7: Part1.5V, S1.Pin_1, S1.Pin_2, S2.Pin_1, S2.Pin_2, S3.Pin_1, S3.Pin_2
  N8: Part1.GND, LED1.common_cathode, R4.Pin_1, R5.Pin_1, R6.Pin_1
  N9: LED1.red_anode, R1.Pin_0
  N10: LED1.green_anode, R2.Pin_0
  N11: LED1.blue_anode, R3.Pin_0
